# Fritzing sketch Schematic (saved by Fritzing 0.9.2b)
breadboards: 1

parts:
  Part1 = Arduino Uno (Rev3)
  R1 = Resistor [tolerance=±5% resistance=330 package=THT]
  R3 = Photocell (LDR) [package=THT]
  R4 = Resistor [tolerance=±5% resistance=10k package=THT]
  IC1 = L293D [package=THT]  # not connected
  LED1 = LED - 3mm [color="White (6500K)" package="3 mm [THT]"]

nets:
  N1: Part1.A0, R3.pin_0, R4.Pin_1
  N2: Part1.5V, R1.Pin_0, R4.Pin_0
  N3: Part1.GND, R3.pin_1, LED1.cathode
  N4: R1.Pin_1, LED1.anode

// code stored in the sketch: Sumobot.ino
// Define pin numbers.
#define TRIGGER 9 // The trigger pin for the ultrasonic sensor.
#define ECHO 10 // The echo pin for the ultrasonic sensor.
#define LDR_PIN A0 // The analog pin for LDR input,

// Define constants.
#define SPEED_OF_SOUND 0.03434 // Speed of sound as STP in cm per microsecond.

// Variables for distance tracking.
long duration;
double distance;

void setup() {
  pinMode(TRIGGER, OUTPUT); // Set the trigger pin as an output.
  pinMode(ECHO, INPUT); // Set the echo pin as an input.
  Serial.begin(9600); // Start the serial communication.
}

// Read the LDR sensor.
void readLDR() {
  int lightLevel = analogRead(LDR_PIN);
  Serial.print("LDR: ");
  Serial.println(lightLevel);
}

// Read the ultrasonic sensor.
void readUltrasonic() {
  // Clear the trigger pin.
  digitalWrite(TRIGGER, LOW);
  delayMicroseconds(2);

  // Set the trigger pin on HIGH state for 10 micro seconds.
  digitalWrite(TRIGGER, HIGH);
  delayMicroseconds(10);
  digitalWrite(TRIGGER, LOW);

  // Read the echo pin.
  duration = pulseIn(ECHO, HIGH); // Sound wave travel time in microseconds.

  distance = duration * SPEED_OF_SOUND / 2.0;

  // Print the distance to the serial monitor.
  Serial.print("Distance: ");
  Serial.println(distance);
  delay(75);
}

void loop() {
  readLDR();
  readUltrasonic();
}
